// Logisim project newpro.circ as structural Verilog: 5 circuits, main circuit main
module main (
);

  wire button_1_out, clock_1_out, cpu_1_jump, not_1_out, register_6_q;
  wire [3:0] disp_1_out_2, disp_1_out_3, disp_1_out_4, disp_1_out_5, disp_1_out_6;
  wire [15:0] counter_1_q, cpu_1_out, n16_reg_1_out_9, n16_reg_1_x1, n16_reg_1_x2, register_2_q,
       register_3_q, register_4_q, register_5_q, register_7_q;
  wire [31:0] register_1_q, rom_1_data;

  Clock clock_1 (.out(clock_1_out));
  Button button_1 (.out(button_1_out));
  Counter #(.width(16), .max('hffff)) counter_1 (
    .load(register_6_q), .D(register_7_q), .count(not_1_out), .Q(counter_1_q), .clk(clock_1_out),
    .clr(button_1_out));  // open: carry
  not not_1 (not_1_out, register_6_q);
  disp disp_1 (
    .in(n16_reg_1_out_9), .out_2(disp_1_out_2), .out_3(disp_1_out_3), .out_4(disp_1_out_4),
    .out_5(disp_1_out_5), .out_6(disp_1_out_6));
  ROM #(.addrWidth(16), .dataWidth(32)) rom_1 (.addr(counter_1_q), .data(rom_1_data), .sel(1'b1));
  Hex_Digit_Display hex_digit_display_1 (.value(disp_1_out_2));  // open: dp
  Register #(.width(32)) register_1 (
    .D(rom_1_data), .Q(register_1_q), .clk(clock_1_out), .clr(button_1_out));  // open: en
  Hex_Digit_Display hex_digit_display_2 (.value(disp_1_out_4));  // open: dp
  Hex_Digit_Display hex_digit_display_3 (.value(disp_1_out_3));  // open: dp
  Hex_Digit_Display hex_digit_display_4 (.value(disp_1_out_6));  // open: dp
  Hex_Digit_Display hex_digit_display_5 (.value(disp_1_out_5));  // open: dp
  _16_reg u_16_reg_1 (
    .NULL(register_1_q[31:16]), .Ax0(register_1_q[3:0]), .Ax1(register_1_q[15:12]), .Ax2(register_1_q[11:8]),
    .x0(register_5_q), .out_9(n16_reg_1_out_9), .ck(clock_1_out), .rst(button_1_out), .x1(n16_reg_1_x1),
    .x2(n16_reg_1_x2));  // open: Ax3, x3
  Register #(.width(16)) register_2 (
    .D(n16_reg_1_x1), .Q(register_2_q), .clk(clock_1_out), .clr(button_1_out));  // open: en
  Register #(.width(16)) register_3 (
    .D(n16_reg_1_x2), .Q(register_3_q), .clk(clock_1_out), .clr(button_1_out));  // open: en
  Register #(.width(16)) register_4 (
    .D(register_1_q[31:16]), .Q(register_4_q), .clk(clock_1_out), .clr(button_1_out));  // open: en
  CPU cpu_1 (.instruct(register_1_q[7:4]), .R1(register_2_q), .R2(register_3_q), .out(cpu_1_out), .jump(cpu_1_jump));
  Register #(.width(16)) register_5 (
    .D(cpu_1_out), .Q(register_5_q), .clk(clock_1_out), .clr(button_1_out));  // open: en
  Register #(.width(1)) register_6 (
    .D(cpu_1_jump), .Q(register_6_q), .clk(clock_1_out), .clr(button_1_out));  // open: en
  Register #(.width(16)) register_7 (
    .D(register_4_q), .Q(register_7_q), .clk(clock_1_out), .clr(button_1_out));  // open: en
  Bit_Extender bit_extender_1 ();  // open: in, out

  // Notes on the sheet:
  //   contents of rom_1 (hex, n*v repeats v):
  //   0 a0000 20050 52 3 2300 3340 13034 4315 1f2533 76 0 336200 80 12000 50010 60 14*0 2000 40050 12061
  //   20010 52 15*0 20062 50 3 3
endmodule

module _16_reg (
  input  [15:0] NULL,
  input  [3:0] Ax0,
  input  [3:0] Ax1,
  input  [3:0] Ax2,
  input  [3:0] Ax3,
  input  [15:0] x0,
  input  ck,
  input  rst,
  output [15:0] out_9,
  output [15:0] x1,
  output [15:0] x2,
  output [15:0] x3
);

  wire decoder_1_out0, decoder_1_out1, decoder_1_out2, decoder_1_out3, decoder_1_out4, decoder_1_out5,
       decoder_1_out6, decoder_1_out7, decoder_1_out8, decoder_1_out9, decoder_1_out10, decoder_1_out11,
       decoder_1_out12, decoder_1_out13, decoder_1_out14, decoder_1_out15;
  wire [15:0] register_3_q, register_4_q, register_5_q, register_6_q, register_7_q, register_8_q,
       register_9_q, register_10_q, register_11_q, register_12_q, register_13_q, register_14_q,
       register_15_q, register_16_q;

  Decoder #(.select(4)) decoder_1 (
    .out0(decoder_1_out0), .out1(decoder_1_out1), .out2(decoder_1_out2), .out3(decoder_1_out3),
    .out4(decoder_1_out4), .out5(decoder_1_out5), .out6(decoder_1_out6), .out7(decoder_1_out7),
    .out8(decoder_1_out8), .out9(decoder_1_out9), .out10(decoder_1_out10), .out11(decoder_1_out11),
    .out12(decoder_1_out12), .out13(decoder_1_out13), .out14(decoder_1_out14), .out15(decoder_1_out15),
    .sel(Ax0));  // open: en
  Register #(.width(16)) register_1 (.D(x0), .en(decoder_1_out0), .clk(ck), .clr(rst));  // open: Q
  Register #(.width(16)) register_2 (.D(x0), .en(decoder_1_out1), .Q(out_9), .clk(ck), .clr(rst));
  Register #(.width(16)) register_3 (.D(x0), .en(decoder_1_out2), .Q(register_3_q), .clk(ck), .clr(rst));
  Register #(.width(16)) register_4 (.D(x0), .en(decoder_1_out3), .Q(register_4_q), .clk(ck), .clr(rst));
  Register #(.width(16)) register_5 (.D(x0), .en(decoder_1_out4), .Q(register_5_q), .clk(ck), .clr(rst));
  Register #(.width(16)) register_6 (.D(x0), .en(decoder_1_out5), .Q(register_6_q), .clk(ck), .clr(rst));
  Register #(.width(16)) register_7 (.D(x0), .en(decoder_1_out6), .Q(register_7_q), .clk(ck), .clr(rst));
  Register #(.width(16)) register_8 (.D(x0), .en(decoder_1_out7), .Q(register_8_q), .clk(ck), .clr(rst));
  Register #(.width(16)) register_9 (.D(x0), .en(decoder_1_out8), .Q(register_9_q), .clk(ck), .clr(rst));
  Register #(.width(16)) register_10 (.D(x0), .en(decoder_1_out9), .Q(register_10_q), .clk(ck), .clr(rst));
  Register #(.width(16)) register_11 (.D(x0), .en(decoder_1_out10), .Q(register_11_q), .clk(ck), .clr(rst));
  Register #(.width(16)) register_12 (.D(x0), .en(decoder_1_out11), .Q(register_12_q), .clk(ck), .clr(rst));
  Register #(.width(16)) register_13 (.D(x0), .en(decoder_1_out12), .Q(register_13_q), .clk(ck), .clr(rst));
  Register #(.width(16)) register_14 (.D(x0), .en(decoder_1_out13), .Q(register_14_q), .clk(ck), .clr(rst));
  Register #(.width(16)) register_15 (.D(x0), .en(decoder_1_out14), .Q(register_15_q), .clk(ck), .clr(rst));
  Register #(.width(16)) register_16 (.D(x0), .en(decoder_1_out15), .Q(register_16_q), .clk(ck), .clr(rst));
  Multiplexer #(.select(4), .width(16)) multiplexer_1 (
    .in0(NULL), .in1(out_9), .in2(register_3_q), .in3(register_4_q), .in4(register_5_q), .in5(register_6_q),
    .in6(register_7_q), .in7(register_8_q), .in8(register_9_q), .in9(register_10_q), .in10(register_11_q),
    .in11(register_12_q), .in12(register_13_q), .in13(register_14_q), .in14(register_15_q),
    .in15(register_16_q), .out(x1), .sel(Ax1));  // open: en
  Multiplexer #(.select(4), .width(16)) multiplexer_2 (
    .in0(NULL), .in1(out_9), .in2(register_3_q), .in3(register_4_q), .in4(register_5_q), .in5(register_6_q),
    .in6(register_7_q), .in7(register_8_q), .in8(register_9_q), .in9(register_10_q), .in10(register_11_q),
    .in11(register_12_q), .in12(register_13_q), .in13(register_14_q), .in14(register_15_q),
    .in15(register_16_q), .out(x2), .sel(Ax2));  // open: en
  Multiplexer #(.select(4), .width(16)) multiplexer_3 (
    .in0(NULL), .in1(out_9), .in2(register_3_q), .in3(register_4_q), .in4(register_5_q), .in5(register_6_q),
    .in6(register_7_q), .in7(register_8_q), .in8(register_9_q), .in9(register_10_q), .in10(register_11_q),
    .in11(register_12_q), .in12(register_13_q), .in13(register_14_q), .in14(register_15_q),
    .in15(register_16_q), .out(x3), .sel(Ax3));  // open: en
endmodule

module CPU (
  input  [3:0] instruct,
  input  [15:0] R1,
  input  [15:0] R2,
  output [15:0] out,
  output jump
);

  wire comparator_1_lt, comparator_2_eq, decoder_1_out1, decoder_1_out2, decoder_1_out3, decoder_1_out4,
       decoder_1_out5, decoder_1_out6, decoder_1_out7, decoder_1_out8;
  wire [15:0] adder_1_out, divider_1_out, multiplier_1_out, subtractor_1_out;

  Decoder #(.select(4)) decoder_1 (
    .out1(decoder_1_out1), .out2(decoder_1_out2), .out3(decoder_1_out3), .out4(decoder_1_out4),
    .out5(decoder_1_out5), .out6(decoder_1_out6), .out7(decoder_1_out7), .out8(decoder_1_out8), .sel(instruct));  // open: out0, out9, out10, out11, out12, out13, out14, out15, en
  assign out = decoder_1_out1 ? adder_1_out : 16'bz;  // Controlled_Buffer controlled_buffer_1
  Adder #(.width(16)) adder_1 (.a(R1), .b(R2), .out(adder_1_out));  // open: cin, cout
  assign out = decoder_1_out2 ? subtractor_1_out : 16'bz;  // Controlled_Buffer controlled_buffer_2
  Subtractor #(.width(16)) subtractor_1 (.a(R1), .b(R2), .out(subtractor_1_out));  // open: bin, bout
  Multiplier #(.width(16)) multiplier_1 (.a(R1), .b(R2), .out(multiplier_1_out));  // open: cin, cout
  assign out = decoder_1_out3 ? multiplier_1_out : 16'bz;  // Controlled_Buffer controlled_buffer_3
  assign out = decoder_1_out4 ? divider_1_out : 16'bz;  // Controlled_Buffer controlled_buffer_4
  Divider #(.width(16)) divider_1 (.a(R1), .b(R2), .out(divider_1_out));  // open: upper, rem
  assign out = decoder_1_out5 ? R1 : 16'bz;  // Controlled_Buffer controlled_buffer_5
  assign jump = decoder_1_out6 ? decoder_1_out6 : 1'bz;  // Controlled_Buffer controlled_buffer_6
  Comparator #(.width(16)) comparator_1 (.a(R1), .b(R2), .lt(comparator_1_lt));  // open: gt, eq
  assign jump = decoder_1_out7 ? comparator_1_lt : 1'bz;  // Controlled_Buffer controlled_buffer_7
  assign jump = decoder_1_out8 ? comparator_2_eq : 1'bz;  // Controlled_Buffer controlled_buffer_8
  Comparator #(.width(16)) comparator_2 (.a(R1), .b(R2), .eq(comparator_2_eq));  // open: gt, lt
  Pull_Resistor pull_resistor_1 (.node(out));
  Pull_Resistor pull_resistor_2 (.node(jump));
endmodule

module disp (
  input  [15:0] in,
  output [3:0] out_2,
  output [3:0] out_3,
  output [3:0] out_4,
  output [3:0] out_5,
  output [3:0] out_6
);

  wire [15:0] divider_2_out, divider_3_out, divider_4_out, divider_5_out, multiplier_1_out, multiplier_2_out,
       multiplier_3_out, multiplier_4_out;
  wire [15:4] divider_1_out, subtractor_1_out, subtractor_2_out, subtractor_3_out, subtractor_4_out;

  Divider #(.width(16)) divider_1 (.a(divider_2_out), .b(16'ha), .out({divider_1_out, out_2}));  // open: upper, rem
  Divider #(.width(16)) divider_2 (.a(divider_3_out), .b(16'ha), .out(divider_2_out));  // open: upper, rem
  Divider #(.width(16)) divider_3 (.a(divider_4_out), .b(16'ha), .out(divider_3_out));  // open: upper, rem
  Divider #(.width(16)) divider_4 (.a(divider_5_out), .b(16'ha), .out(divider_4_out));  // open: upper, rem
  Divider #(.width(16)) divider_5 (.a(in), .b(16'ha), .out(divider_5_out));  // open: upper, rem
  Multiplier #(.width(16)) multiplier_1 (.a(divider_2_out), .b(16'ha), .out(multiplier_1_out));  // open: cin, cout
  Multiplier #(.width(16)) multiplier_2 (.a(divider_3_out), .b(16'ha), .out(multiplier_2_out));  // open: cin, cout
  Multiplier #(.width(16)) multiplier_3 (.a(divider_4_out), .b(16'ha), .out(multiplier_3_out));  // open: cin, cout
  Multiplier #(.width(16)) multiplier_4 (.a(divider_5_out), .b(16'ha), .out(multiplier_4_out));  // open: cin, cout
  Subtractor #(.width(16)) subtractor_1 (
    .a(divider_3_out), .b(multiplier_1_out), .out({subtractor_1_out, out_3}));  // open: bin, bout
  Subtractor #(.width(16)) subtractor_2 (
    .a(divider_4_out), .b(multiplier_2_out), .out({subtractor_2_out, out_4}));  // open: bin, bout
  Subtractor #(.width(16)) subtractor_3 (
    .a(divider_5_out), .b(multiplier_3_out), .out({subtractor_3_out, out_5}));  // open: bin, bout
  Subtractor #(.width(16)) subtractor_4 (
    .a(in), .b(multiplier_4_out), .out({subtractor_4_out, out_6}));  // open: bin, bout
endmodule

module memory (
  input  send,
  input  [15:0] address,
  input  [15:0] value,
  input  rst,
  input  ck,
  output [15:0] retval
);

  wire not_1_out, register_1_q, register_4_q;
  wire [15:0] controlled_buffer_1_out, register_2_q, register_3_q, register_5_q, register_6_q, register_7_q;

  Register #(.width(1)) register_1 (.D(send), .Q(register_1_q), .clk(ck), .clr(rst));  // open: en
  Register #(.width(16)) register_2 (.D(address), .Q(register_2_q), .clk(ck), .clr(rst));  // open: en
  Register #(.width(16)) register_3 (.D(value), .Q(register_3_q), .clk(ck), .clr(rst));  // open: en
  Register #(.width(1)) register_4 (.D(register_1_q), .Q(register_4_q), .clk(ck), .clr(rst));  // open: en
  not not_1 (not_1_out, register_4_q);
  Register #(.width(16)) register_5 (.D(register_2_q), .Q(register_5_q), .clk(ck), .clr(rst));  // open: en
  Register #(.width(16)) register_6 (.D(register_3_q), .Q(register_6_q), .clk(ck), .clr(rst));  // open: en
  assign controlled_buffer_1_out = register_4_q ? register_6_q : 16'bz;  // Controlled_Buffer controlled_buffer_1
  RAM #(.addrWidth(16), .dataWidth(16)) ram_1 (
    .addr(register_5_q), .data(controlled_buffer_1_out), .sel(1'b1), .clk(ck), .ld(not_1_out), .clr(rst));
  Register #(.width(16)) register_7 (.D(controlled_buffer_1_out), .Q(register_7_q), .clk(ck), .clr(rst));  // open: en
  Register #(.width(16)) register_8 (.D(register_7_q), .Q(retval), .clk(ck), .clr(rst));  // open: en
  // Buffer buffer_1 is placed but not wired
endmodule
