// Logisim project one.circ as structural Verilog: 4 circuits, main circuit main
module main (
);

  wire decoder_1_out1, decoder_1_out2, decoder_1_out3, decoder_1_out4, decoder_1_out5, decoder_1_out6,
       decoder_1_out7, decoder_1_out8, decoder_1_out9, decoder_1_out10, decoder_1_out11, decoder_1_out12,
       decoder_1_out13, decoder_1_out14, decoder_1_out15, undriven_2, undriven_3;
  wire [1:0] controlled_buffer_2_out, register_3_q;
  wire [3:0] register_1_q_2, register_2_q;
  wire [15:0] memspot_1_out, n16regs_1_x1, n16regs_1_x2, register_1_q, register_1_q_3, register_4_q,
       register_4_q_2;
  wire [31:0] rom_1_data;
  wire [31:16] undriven;

  memspot memspot_1 (
    .add(register_3_q[0]), .sub(register_3_q[1]), .\input (register_4_q), .ck(undriven_2),
    .reset(undriven_3), .out(memspot_1_out));
  ROM #(.addrWidth(16), .dataWidth(32)) rom_1 (.addr(memspot_1_out), .data(rom_1_data));  // open: sel
  _16regs u_16regs_1 (
    .CX0(1'b1), .LX0(register_1_q[3:0]), .X0(register_4_q_2), .LX1(register_1_q[15:12]),
    .LX2(register_1_q_2), .overload(register_1_q_3), .ck(undriven_2), .reset(undriven_3), .X1(n16regs_1_x1),
    .X2(n16regs_1_x2));
  Register #(.width(32)) register_1 (
    .D(rom_1_data), .Q({register_1_q_3, register_1_q[15:12], register_1_q_2, register_1_q[7:0]}),
    .clk(undriven_2), .clr(undriven_3));  // open: en
  Decoder #(.select(4)) decoder_1 (
    .out1(decoder_1_out1), .out2(decoder_1_out2), .out3(decoder_1_out3), .out4(decoder_1_out4),
    .out5(decoder_1_out5), .out6(decoder_1_out6), .out7(decoder_1_out7), .out8(decoder_1_out8),
    .out9(decoder_1_out9), .out10(decoder_1_out10), .out11(decoder_1_out11), .out12(decoder_1_out12),
    .out13(decoder_1_out13), .out14(decoder_1_out14), .out15(decoder_1_out15), .sel(register_2_q));  // open: out0, en
  Register #(.width(4)) register_2 (
    .D(register_1_q[7:4]), .Q(register_2_q), .clk(undriven_2), .clr(undriven_3));  // open: en
  Register #(.width(2)) register_3 (
    .D(controlled_buffer_2_out), .Q(register_3_q), .clk(undriven_2), .clr(undriven_3));  // open: en
  Register #(.width(32)) register_4 (
    .D({undriven, n16regs_1_x1}), .Q({register_4_q_2, register_4_q}), .clk(undriven_2), .clr(undriven_3));  // open: en
  assign controlled_buffer_2_out[1] = decoder_1_out1 ? decoder_1_out1 : 1'bz;  // Controlled_Buffer controlled_buffer_1
  assign controlled_buffer_2_out[0] = decoder_1_out2 ? decoder_1_out2 : 1'bz;  // Controlled_Buffer controlled_buffer_2
  Pull_Resistor pull_resistor_1 (.node(controlled_buffer_2_out[0]));
  Pull_Resistor pull_resistor_2 (.node(controlled_buffer_2_out[1]));
  D_Flip_Flop d_ff_1 ();  // open: clk, D, Q, Qn, preset, en, reset

  // Notes on the sheet:
  //   contents of rom_1 (hex, n*v repeats v):
  //   ddaada
endmodule

module _4regs (
  input  esto,
  input  [15:0] datain,
  input  [1:0] select,
  input  control1,
  input  in_5,
  input  in_6,
  input  [1:0] A1,
  input  control2,
  input  [1:0] A2,
  output [15:0] out1,
  output [15:0] out2
);

  wire decoder_1_out0, decoder_1_out1, decoder_1_out2, decoder_1_out3, decoder_2_out0, decoder_2_out1,
       decoder_2_out2, decoder_2_out3, decoder_3_out0, decoder_3_out1, decoder_3_out2, decoder_3_out3;
  wire [15:0] register_1_q, register_2_q, register_3_q, register_4_q;

  Decoder #(.select(2), .disabled(0)) decoder_1 (
    .out0(decoder_1_out0), .out1(decoder_1_out1), .out2(decoder_1_out2), .out3(decoder_1_out3), .sel(select),
    .en(esto));
  Register #(.width(16)) register_1 (.D(datain), .en(decoder_1_out0), .Q(register_1_q), .clk(in_5), .clr(in_6));
  Register #(.width(16)) register_2 (.D(datain), .en(decoder_1_out1), .Q(register_2_q), .clk(in_5), .clr(in_6));
  Register #(.width(16)) register_3 (.D(datain), .en(decoder_1_out2), .Q(register_3_q), .clk(in_5), .clr(in_6));
  Register #(.width(16)) register_4 (.D(datain), .en(decoder_1_out3), .Q(register_4_q), .clk(in_5), .clr(in_6));
  Decoder #(.select(2), .disabled(0)) decoder_2 (
    .out0(decoder_2_out0), .out1(decoder_2_out1), .out2(decoder_2_out2), .out3(decoder_2_out3), .sel(A1),
    .en(control1));
  assign out1 = decoder_2_out0 ? register_1_q : 16'bz;  // Controlled_Buffer controlled_buffer_1
  assign out1 = decoder_2_out1 ? register_2_q : 16'bz;  // Controlled_Buffer controlled_buffer_2
  assign out1 = decoder_2_out2 ? register_3_q : 16'bz;  // Controlled_Buffer controlled_buffer_3
  assign out1 = decoder_2_out3 ? register_4_q : 16'bz;  // Controlled_Buffer controlled_buffer_4
  Decoder #(.select(2), .disabled(0)) decoder_3 (
    .out0(decoder_3_out0), .out1(decoder_3_out1), .out2(decoder_3_out2), .out3(decoder_3_out3), .sel(A2),
    .en(control2));
  assign out2 = decoder_3_out0 ? register_1_q : 16'bz;  // Controlled_Buffer controlled_buffer_5
  assign out2 = decoder_3_out1 ? register_2_q : 16'bz;  // Controlled_Buffer controlled_buffer_6
  assign out2 = decoder_3_out2 ? register_3_q : 16'bz;  // Controlled_Buffer controlled_buffer_7
  assign out2 = decoder_3_out3 ? register_4_q : 16'bz;  // Controlled_Buffer controlled_buffer_8
endmodule

module _16regs (
  input  CX0,
  input  [3:0] LX0,
  input  [15:0] X0,
  input  [3:0] LX1,
  input  ck,
  input  reset,
  input  [3:0] LX2,
  input  [15:0] overload,
  output [15:0] X1,
  output [15:0] X2
);

  wire and_1_out, and_2_out, decoder_1_out0, decoder_1_out1, decoder_1_out2, decoder_1_out3, decoder_2_out0,
       decoder_2_out1, decoder_2_out2, decoder_2_out3, decoder_3_out0, decoder_3_out1, decoder_3_out2,
       decoder_3_out3, not_3_out, not_4_out;
  wire [3:0] not_1_out, not_2_out;
  wire [15:0] multiplexer_1_out, multiplexer_2_out, n4regs_1_out1, n4regs_1_out2;

  assign not_1_out = ~LX1;  // NOT_Gate not_1, 4 bits wide
  assign not_2_out = ~LX2;  // NOT_Gate not_2, 4 bits wide
  and and_1 (and_1_out, not_1_out[0], not_1_out[1], not_1_out[2], not_1_out[3]);
  and and_2 (and_2_out, not_2_out[0], not_2_out[1], not_2_out[2], not_2_out[3]);
  Decoder #(.select(2), .disabled(0)) decoder_1 (
    .out0(decoder_1_out0), .out1(decoder_1_out1), .out2(decoder_1_out2), .out3(decoder_1_out3),
    .sel(LX0[1:0]), .en(CX0));
  not not_3 (not_3_out, and_1_out);
  Decoder #(.select(2), .disabled(0)) decoder_2 (
    .out0(decoder_2_out0), .out1(decoder_2_out1), .out2(decoder_2_out2), .out3(decoder_2_out3),
    .sel(LX1[1:0]), .en(not_3_out));
  not not_4 (not_4_out, and_2_out);
  Decoder #(.select(2), .disabled(0)) decoder_3 (
    .out0(decoder_3_out0), .out1(decoder_3_out1), .out2(decoder_3_out2), .out3(decoder_3_out3),
    .sel(LX2[1:0]), .en(not_4_out));
  _4regs u_4regs_1 (
    .esto(decoder_1_out0), .datain(X0), .select(LX0[3:2]), .control1(decoder_2_out0), .A1(LX1[3:2]),
    .control2(decoder_3_out0), .A2(LX2[3:2]), .in_5(ck), .in_6(reset), .out1(n4regs_1_out1),
    .out2(n4regs_1_out2));
  _4regs u_4regs_2 (
    .esto(decoder_1_out1), .datain(X0), .select(LX0[3:2]), .control1(decoder_2_out1), .A1(LX1[3:2]),
    .control2(decoder_3_out1), .A2(LX2[3:2]), .in_5(ck), .in_6(reset), .out1(n4regs_1_out1),
    .out2(n4regs_1_out2));
  _4regs u_4regs_3 (
    .esto(decoder_1_out2), .datain(X0), .select(LX0[3:2]), .control1(decoder_2_out2), .A1(LX1[3:2]),
    .control2(decoder_3_out2), .A2(LX2[3:2]), .in_5(ck), .in_6(reset), .out1(n4regs_1_out1),
    .out2(n4regs_1_out2));
  _4regs u_4regs_4 (
    .esto(decoder_1_out3), .datain(X0), .select(LX0[3:2]), .control1(decoder_2_out3), .A1(LX1[3:2]),
    .control2(decoder_3_out3), .A2(LX2[3:2]), .in_5(ck), .in_6(reset), .out1(n4regs_1_out1),
    .out2(n4regs_1_out2));
  Multiplexer #(.width(16)) multiplexer_1 (
    .in0(overload), .in1(n4regs_1_out1), .out(multiplexer_1_out), .sel(and_1_out));  // open: en
  Multiplexer #(.width(16)) multiplexer_2 (
    .in0(overload), .in1(n4regs_1_out2), .out(multiplexer_2_out), .sel(and_2_out));  // open: en
  Register #(.width(16)) register_1 (.D(multiplexer_1_out), .Q(X1), .clk(ck), .clr(reset));  // open: en
  Register #(.width(16)) register_2 (.D(multiplexer_2_out), .Q(X2), .clk(ck), .clr(reset));  // open: en
endmodule

module memspot (
  input  add,
  input  sub,
  input  [15:0] \input ,
  input  ck,
  input  reset,
  output [15:0] out
);

  wire nor_1_out;
  wire [15:0] adder_1_out, controlled_buffer_1_out, subtractor_1_out;

  Subtractor #(.width(16)) subtractor_1 (.a(out), .b(\input ), .out(subtractor_1_out));  // open: bin, bout
  nor nor_1 (nor_1_out, add, sub);
  assign controlled_buffer_1_out = add ? adder_1_out : 16'bz;  // Controlled_Buffer controlled_buffer_1
  Adder #(.width(16)) adder_1 (.a(out), .b(\input ), .out(adder_1_out));  // open: cin, cout
  assign controlled_buffer_1_out = sub ? subtractor_1_out : 16'bz;  // Controlled_Buffer controlled_buffer_2
  Counter #(.width(16), .max('hffff)) counter_1 (
    .D(controlled_buffer_1_out), .count(nor_1_out), .Q(out), .clk(ck), .clr(reset));  // open: load, carry
endmodule
